// Digital circuit 64bit_register.dig as structural Verilog
module _64bit_register (
  input  [63:0] D,
  input  CLR,
  input  CLK,
  input  EN,
  output [63:0] Q
);

  wire or_1_out;
  wire [63:0] multiplexer_1_out;

  Multiplexer #(.Bits(64)) multiplexer_1 (.sel(CLR), .in_0(D), .in_1({64{1'b0}}), .out(multiplexer_1_out));
  or or_1 (or_1_out, CLR, CLK);
  Register #(.Bits(64)) register_1 (.D(multiplexer_1_out), .C(or_1_out), .en(EN), .Q(Q));
endmodule
