// Digital circuit alu.dig as structural Verilog
module alu (
  input  [63:0] A,
  input  [63:0] B,
  input  [3:0] ALUop,
  output [63:0] R
);

  wire [63:0] add_1_s, and_1_out, barrelshifter_1_out, barrelshifter_2_out, div_1_q, mul_1_mul, or_1_out,
       sub_1_s;

  assign and_1_out = A & B;  // And and_1, 64 bits wide
  assign or_1_out = A | B;  // Or or_1, 64 bits wide
  Add #(.Bits(64)) add_1 (.a(A), .b(B), .c_i(1'b0), .s(add_1_s));  // open: c_o
  Sub #(.Bits(64)) sub_1 (.a(A), .b(B), .c_i(1'b0), .s(sub_1_s));  // open: c_o
  Mul #(.Bits(32)) mul_1 (.a(A[31:0]), .b(B[31:0]), .mul(mul_1_mul));
  Div #(.Bits(64)) div_1 (.a(A), .b(B), .q(div_1_q));  // open: r
  BarrelShifter #(.Bits(64), .barrelSigned("true")) barrelshifter_1 (.in(A), .shift(B[7:0]), .out(barrelshifter_1_out));
  BarrelShifter #(.Bits(64), .barrelSigned("true"), .direction("right")) barrelshifter_2 (
    .in(A), .shift(B[7:0]), .out(barrelshifter_2_out));
  Multiplexer #(.Selector_Bits(4), .Bits(64)) multiplexer_1 (
    .sel(ALUop), .in_0(add_1_s), .in_1(sub_1_s), .in_2(mul_1_mul), .in_3(div_1_q),
    .in_4(barrelshifter_1_out), .in_5(barrelshifter_2_out), .in_6({B[51:0], {12{1'b0}}}), .in_7(and_1_out),
    .in_8(or_1_out), .in_9({64{1'b0}}), .in_10({64{1'b0}}), .in_11({64{1'b0}}), .in_12({64{1'b0}}),
    .in_13({64{1'b0}}), .in_14({64{1'b0}}), .in_15({64{1'b0}}), .out(R));
endmodule
