// Digital circuit bcu.dig as structural Verilog
module bcu (
  input  [63:0] A,
  input  [63:0] B,
  input  [2:0] BROp,
  input  PCsel,
  output O
);

  wire comparator_1_lt, comparator_2_eq, comparator_3_eq, comparator_3_gt, comparator_4_eq,
       multiplexer_1_out, not_1_out, or_1_out;

  Comparator #(.Bits(64)) comparator_1 (.a(A), .b(B), .lt(comparator_1_lt));  // open: gt, eq
  Comparator #(.Bits(64)) comparator_2 (.a(A), .b(B), .eq(comparator_2_eq));  // open: gt, lt
  Comparator #(.Bits(64)) comparator_3 (.a(A), .b(B), .gt(comparator_3_gt), .eq(comparator_3_eq));  // open: lt
  Comparator #(.Bits(64)) comparator_4 (.a(A), .b(B), .eq(comparator_4_eq));  // open: gt, lt
  or or_1 (or_1_out, comparator_3_gt, comparator_3_eq);
  not not_1 (not_1_out, comparator_4_eq);
  Multiplexer #(.Selector_Bits(3)) multiplexer_1 (
    .sel(BROp), .in_0(1'b0), .in_1(comparator_1_lt), .in_2(comparator_2_eq), .in_3(or_1_out),
    .in_4(not_1_out), .in_5(1'b0), .in_6(1'b0), .in_7(1'b0), .out(multiplexer_1_out));
  or or_2 (O, PCsel, multiplexer_1_out);

  // Notes on the sheet:
  //   blt
  //   beq
  //   bge
  //   bne
endmodule
