// Digital circuit instruction-decoder-part2.dig as structural Verilog
module instruction_decoder_part2 (
  input  [31:0] IW,
  output WDsel,
  output PCsel,
  output [2:0] ALUSrcB,
  output ALUSrcA,
  output [3:0] ALUOp,
  output RFW,
  output [2:0] BROp,
  output [1:0] MSZ,
  output ST,
  output LD,
  output MR
);

  wire b1, b2, b3, b4, comparator_1_eq, comparator_2_eq, comparator_3_eq, comparator_4_eq, comparator_5_eq,
       comparator_6_eq, comparator_7_eq, comparator_8_eq, comparator_9_eq, comparator_10_eq,
       comparator_11_eq, comparator_12_eq, comparator_13_eq, comparator_14_eq, comparator_15_eq,
       comparator_16_eq, comparator_17_eq, comparator_18_eq, comparator_19_eq, comparator_20_eq,
       comparator_21_eq, comparator_22_eq, comparator_23_eq, comparator_24_eq, comparator_25_eq,
       comparator_26_eq, comparator_27_eq, comparator_28_eq, comparator_29_eq, comparator_31_eq,
       comparator_32_eq, comparator_33_eq, comparator_34_eq, comparator_35_eq, comparator_36_eq,
       comparator_37_eq, comparator_38_eq, comparator_39_eq, comparator_40_eq, comparator_41_eq,
       comparator_42_eq, comparator_43_eq, comparator_44_eq, comparator_45_eq, comparator_47_eq,
       comparator_48_eq, comparator_49_eq, comparator_50_eq, comparator_51_eq, comparator_52_eq,
       comparator_53_eq, comparator_54_eq, i1, i2, i3, i4, i5, i6, j1, j2, r1, r2, r3, r4, r5, r6, r7, r8,
       s1, s2, s3, u1;
  wire [4:0] priorityencoder_1_num;

  Comparator #(.Bits(7)) comparator_1 (.a(IW[6:0]), .b(7'b0110011), .eq(comparator_1_eq));  // open: gt, lt
  Comparator #(.Bits(7)) comparator_2 (.a(IW[6:0]), .b(7'b0110011), .eq(comparator_2_eq));  // open: gt, lt
  Comparator #(.Bits(7)) comparator_3 (.a(IW[6:0]), .b(7'b0110011), .eq(comparator_3_eq));  // open: gt, lt
  Comparator #(.Bits(7)) comparator_4 (.a(IW[6:0]), .b(7'b0110011), .eq(comparator_4_eq));  // open: gt, lt
  Comparator #(.Bits(7)) comparator_5 (.a(IW[6:0]), .b(7'b0110011), .eq(comparator_5_eq));  // open: gt, lt
  Comparator #(.Bits(7)) comparator_6 (.a(IW[6:0]), .b(7'b0110011), .eq(comparator_6_eq));  // open: gt, lt
  Comparator #(.Bits(3)) comparator_7 (.a(IW[14:12]), .b(3'b000), .eq(comparator_7_eq));  // open: gt, lt
  Comparator #(.Bits(7)) comparator_8 (.a(IW[31:25]), .b({7{1'b0}}), .eq(comparator_8_eq));  // open: gt, lt
  Comparator #(.Bits(3)) comparator_9 (.a(IW[14:12]), .b(3'b001), .eq(comparator_9_eq));  // open: gt, lt
  Comparator #(.Bits(7)) comparator_10 (.a(IW[31:25]), .b({7{1'b0}}), .eq(comparator_10_eq));  // open: gt, lt
  Comparator #(.Bits(3)) comparator_11 (.a(IW[14:12]), .b(3'b101), .eq(comparator_11_eq));  // open: gt, lt
  Comparator #(.Bits(7)) comparator_12 (.a(IW[31:25]), .b({7{1'b0}}), .eq(comparator_12_eq));  // open: gt, lt
  Comparator #(.Bits(3)) comparator_13 (.a(IW[14:12]), .b(3'b000), .eq(comparator_13_eq));  // open: gt, lt
  Comparator #(.Bits(7)) comparator_14 (.a(IW[31:25]), .b(7'b0000001), .eq(comparator_14_eq));  // open: gt, lt
  Comparator #(.Bits(3)) comparator_15 (.a(IW[14:12]), .b(3'b000), .eq(comparator_15_eq));  // open: gt, lt
  Comparator #(.Bits(7)) comparator_16 (.a(IW[31:25]), .b(7'b0100000), .eq(comparator_16_eq));  // open: gt, lt
  Comparator #(.Bits(3)) comparator_17 (.a(IW[14:12]), .b(3'b111), .eq(comparator_17_eq));  // open: gt, lt
  Comparator #(.Bits(7)) comparator_18 (.a(IW[31:25]), .b({7{1'b0}}), .eq(comparator_18_eq));  // open: gt, lt
  and and_1 (r1, comparator_1_eq, comparator_7_eq, comparator_8_eq);
  and and_2 (r2, comparator_2_eq, comparator_9_eq, comparator_10_eq);
  and and_3 (r3, comparator_3_eq, comparator_11_eq, comparator_12_eq);
  and and_4 (r4, comparator_4_eq, comparator_13_eq, comparator_14_eq);
  and and_5 (r5, comparator_5_eq, comparator_15_eq, comparator_16_eq);
  and and_6 (r6, comparator_6_eq, comparator_17_eq, comparator_18_eq);
  Comparator #(.Bits(7)) comparator_19 (.a(IW[6:0]), .b(7'b0010011), .eq(comparator_19_eq));  // open: gt, lt
  Comparator #(.Bits(7)) comparator_20 (.a(IW[6:0]), .b(7'b0010011), .eq(comparator_20_eq));  // open: gt, lt
  Comparator #(.Bits(3)) comparator_21 (.a(IW[14:12]), .b(3'b001), .eq(comparator_21_eq));  // open: gt, lt
  Comparator #(.Bits(7)) comparator_22 (.a(IW[6:0]), .b(7'b0010011), .eq(comparator_22_eq));  // open: gt, lt
  Comparator #(.Bits(3)) comparator_23 (.a(IW[14:12]), .b(3'b101), .eq(comparator_23_eq));  // open: gt, lt
  Comparator #(.Bits(7)) comparator_24 (.a(IW[6:0]), .b(7'b0000011), .eq(comparator_24_eq));  // open: gt, lt
  Comparator #(.Bits(3)) comparator_25 (.a(IW[14:12]), .b(3'b011), .eq(comparator_25_eq));  // open: gt, lt
  Comparator #(.Bits(7)) comparator_26 (.a(IW[6:0]), .b(7'b0000011), .eq(comparator_26_eq));  // open: gt, lt
  Comparator #(.Bits(3)) comparator_27 (.a(IW[14:12]), .b(3'b000), .eq(comparator_27_eq));  // open: gt, lt
  Comparator #(.Bits(7)) comparator_28 (.a(IW[6:0]), .b(7'b0000011), .eq(comparator_28_eq));  // open: gt, lt
  Comparator #(.Bits(3)) comparator_29 (.a(IW[14:12]), .b(3'b010), .eq(comparator_29_eq));  // open: gt, lt
  Comparator #(.Bits(7)) comparator_30 (.a(IW[6:0]), .b(7'b1101111), .eq(j1));  // open: gt, lt
  Comparator #(.Bits(7)) comparator_31 (.a(IW[6:0]), .b(7'b1100111), .eq(comparator_31_eq));  // open: gt, lt
  Comparator #(.Bits(3)) comparator_32 (.a(IW[14:12]), .b(3'b000), .eq(comparator_32_eq));  // open: gt, lt
  Comparator #(.Bits(3)) comparator_33 (.a(IW[14:12]), .b(3'b000), .eq(comparator_33_eq));  // open: gt, lt
  and and_7 (i1, comparator_19_eq, comparator_33_eq);
  and and_8 (i2, comparator_20_eq, comparator_21_eq);
  and and_9 (i3, comparator_22_eq, comparator_23_eq);
  and and_10 (i4, comparator_24_eq, comparator_25_eq);
  and and_11 (i5, comparator_26_eq, comparator_27_eq);
  and and_12 (i6, comparator_28_eq, comparator_29_eq);
  and and_13 (j2, comparator_31_eq, comparator_32_eq);
  Comparator #(.Bits(7)) comparator_34 (.a(IW[6:0]), .b(7'b1100011), .eq(comparator_34_eq));  // open: gt, lt
  Comparator #(.Bits(3)) comparator_35 (.a(IW[14:12]), .b(3'b100), .eq(comparator_35_eq));  // open: gt, lt
  Comparator #(.Bits(7)) comparator_36 (.a(IW[6:0]), .b(7'b1100011), .eq(comparator_36_eq));  // open: gt, lt
  Comparator #(.Bits(3)) comparator_37 (.a(IW[14:12]), .b(3'b000), .eq(comparator_37_eq));  // open: gt, lt
  Comparator #(.Bits(7)) comparator_38 (.a(IW[6:0]), .b(7'b1100011), .eq(comparator_38_eq));  // open: gt, lt
  Comparator #(.Bits(3)) comparator_39 (.a(IW[14:12]), .b(3'b101), .eq(comparator_39_eq));  // open: gt, lt
  Comparator #(.Bits(7)) comparator_40 (.a(IW[6:0]), .b(7'b0100011), .eq(comparator_40_eq));  // open: gt, lt
  Comparator #(.Bits(3)) comparator_41 (.a(IW[14:12]), .b(3'b011), .eq(comparator_41_eq));  // open: gt, lt
  Comparator #(.Bits(7)) comparator_42 (.a(IW[6:0]), .b(7'b0100011), .eq(comparator_42_eq));  // open: gt, lt
  Comparator #(.Bits(3)) comparator_43 (.a(IW[14:12]), .b(3'b000), .eq(comparator_43_eq));  // open: gt, lt
  Comparator #(.Bits(7)) comparator_44 (.a(IW[6:0]), .b(7'b0100011), .eq(comparator_44_eq));  // open: gt, lt
  Comparator #(.Bits(3)) comparator_45 (.a(IW[14:12]), .b(3'b010), .eq(comparator_45_eq));  // open: gt, lt
  Comparator #(.Bits(7)) comparator_46 (.a(IW[6:0]), .b(7'b0110111), .eq(u1));  // open: gt, lt
  Comparator #(.Bits(7)) comparator_47 (.a(IW[6:0]), .b(7'b1100011), .eq(comparator_47_eq));  // open: gt, lt
  Comparator #(.Bits(3)) comparator_48 (.a(IW[14:12]), .b(3'b001), .eq(comparator_48_eq));  // open: gt, lt
  and and_14 (b1, comparator_34_eq, comparator_35_eq);
  and and_15 (b2, comparator_36_eq, comparator_37_eq);
  and and_16 (b3, comparator_38_eq, comparator_39_eq);
  and and_17 (s1, comparator_40_eq, comparator_41_eq);
  and and_18 (s2, comparator_42_eq, comparator_43_eq);
  and and_19 (s3, comparator_44_eq, comparator_45_eq);
  and and_20 (b4, comparator_47_eq, comparator_48_eq);
  PriorityEncoder #(.Selector_Bits(5)) priorityencoder_1 (
    .in0(i1), .in1(r1), .in2(r2), .in3(r3), .in4(r4), .in5(r5), .in6(r6), .in7(i2), .in8(i3), .in9(i4),
    .in10(i5), .in11(i6), .in12(j1), .in13(j2), .in14(b1), .in15(b2), .in16(b3), .in17(s1), .in18(s2),
    .in19(s3), .in20(u1), .in21(b4), .in22(r7), .in23(r8), .in24(1'b0), .in25(1'b0), .in26(1'b0),
    .in27(1'b0), .in28(1'b0), .in29(1'b0), .in30(1'b0), .in31(1'b0), .num(priorityencoder_1_num));  // open: any
  Comparator #(.Bits(7)) comparator_49 (.a(IW[6:0]), .b(7'b0111011), .eq(comparator_49_eq));  // open: gt, lt
  Comparator #(.Bits(7)) comparator_50 (.a(IW[6:0]), .b(7'b0110011), .eq(comparator_50_eq));  // open: gt, lt
  Comparator #(.Bits(3)) comparator_51 (.a(IW[14:12]), .b(3'b000), .eq(comparator_51_eq));  // open: gt, lt
  Comparator #(.Bits(7)) comparator_52 (.a(IW[31:25]), .b({7{1'b0}}), .eq(comparator_52_eq));  // open: gt, lt
  Comparator #(.Bits(3)) comparator_53 (.a(IW[14:12]), .b(3'b110), .eq(comparator_53_eq));  // open: gt, lt
  Comparator #(.Bits(7)) comparator_54 (.a(IW[31:25]), .b({7{1'b0}}), .eq(comparator_54_eq));  // open: gt, lt
  ROM #(.AddrBits(5), .Bits(19)) rom_1 (
    .A(priorityencoder_1_num), .sel(1'b1),
    .D({MR, LD, ST, MSZ, BROp, RFW, ALUOp, ALUSrcA, ALUSrcB, PCsel, WDsel}));
  and and_21 (r8, comparator_49_eq, comparator_51_eq, comparator_52_eq);
  and and_22 (r7, comparator_50_eq, comparator_53_eq, comparator_54_eq);

  // Other names for the same wires on the sheet: opcode[6:0] = IW[6:0]; funct3[2:0] = IW[14:12];
  //   funct7[6:0] = IW[31:25]

  // Notes on the sheet:
  //   r-type
  //   add
  //   sll
  //   srl
  //   mul
  //   sub
  //   and
  //   i-type
  //   ld
  //   lb
  //   lw
  //   j-type
  //   i-type-jalr
  //   jalr
  //   b-type
  //   blt
  //   beq
  //   bge
  //   s-type
  //   sd
  //   sb
  //   sw
  //   u-type
  //   bne
  //   INUM
  //   addw
  //   or
  //   contents of rom_1 (hex, n*v repeats v):
  //   404,400,500,540,480,440,5c0,504,544,6c404,64404,68404,42b,40b
  //   ,831,1031,1831,3c00c,3400c,3800c,414,2031,600,4c0
endmodule
