// Digital circuit instruction_decoder.dig as structural Verilog
module instruction_decoder (
  input  [31:0] IW,
  output ALUSrcB,
  output [2:0] ALUOp,
  output RFW
);

  wire and_1_out, and_2_out, comparator_1_eq, comparator_2_eq, comparator_3_eq, comparator_4_eq,
       comparator_5_eq, priorityencoder_1_num;

  Comparator #(.Bits(7)) comparator_1 (.a(IW[6:0]), .b(7'b0001001), .eq(comparator_1_eq));  // open: gt, lt
  Comparator #(.Bits(3)) comparator_2 (.a(IW[14:12]), .b(3'b000), .eq(comparator_2_eq));  // open: gt, lt
  Comparator #(.Bits(7)) comparator_3 (.a(IW[6:0]), .b(7'b0110011), .eq(comparator_3_eq));  // open: gt, lt
  Comparator #(.Bits(3)) comparator_4 (.a(IW[14:12]), .b(3'b000), .eq(comparator_4_eq));  // open: gt, lt
  Comparator #(.Bits(7)) comparator_5 (.a(IW[31:25]), .b({7{1'b0}}), .eq(comparator_5_eq));  // open: gt, lt
  and and_1 (and_1_out, comparator_1_eq, comparator_2_eq);
  and and_2 (and_2_out, comparator_3_eq, comparator_4_eq, comparator_5_eq);
  PriorityEncoder priorityencoder_1 (.in0(and_1_out), .in1(and_2_out), .num(priorityencoder_1_num));  // open: any
  ROM #(.AddrBits(1), .Bits(5)) rom_1 (.A(priorityencoder_1_num), .sel(1'b1), .D({RFW, ALUOp, ALUSrcB}));

  // Other names for the same wires on the sheet: opcode[6:0] = IW[6:0]; funct3[2:0] = IW[14:12];
  //   funct7[6:0] = IW[31:25]

  // Notes on the sheet:
  //   i-type
  //   add
  //   r-type
  //   INUM
  //   contents of rom_1 (hex, n*v repeats v):
  //   11,10
endmodule
