// Digital circuit project06.dig as structural Verilog
module project06 (
  input  [4:0] PROG,
  input  CLK,
  input  EN,
  input  CLR,
  output [63:0] A0,
  output [63:0] A1,
  output [63:0] A2,
  output DONE
);

  wire ALUSrcA, and_2_out, bcu_1_o, CLK_t, LD, MR, PCsel, RFW, ST, WDsel;
  wire [1:0] BROp, MSZ;
  wire [2:0] ALUOp, ALUSrcB;
  wire [4:0] rd, rs1, rs2;
  wire [31:0] iw;
  wire [63:0] A, add_1_s, alu_1_r, B, imm_B, imm_I, imm_J, imm_S, imm_U, multiplexer_1_out,
       multiplexer_2_out, multiplexer_3_out, multiplexer_4_out, multiplexer_5_out, PC, ramdualport_1_d,
       read_1_dcur, read_1_dout, write_1_d, x0, x1, x2, x3, x4, x5, x6, x7, x8, x9, x13, x14, x15, x16, x17,
       x18, x19, x20, x21, x22, x23, x24, x25, x26, x27, x28, x29, x30, x31;

  // Probe on BROp
  // Probe on A
  bcu bcu_1 (.PCsel(PCsel), .BROp(BROp), .A(A), .B(B), .O(bcu_1_o));
  // Probe on B
  Multiplexer #(.Bits(64)) multiplexer_1 (
    .sel(bcu_1_o), .in_0(add_1_s), .in_1(multiplexer_5_out), .out(multiplexer_1_out));
  // Probe on iw
  and and_1 (CLK_t, CLK, ~DONE);  // And
  Comparator #(.Bits(32)) comparator_1 (.a(iw), .b(32'hc0001073), .eq(DONE));  // open: gt, lt
  LED led_1 (.in(DONE));
  _64bit_register _64bit_register_1 (.D(multiplexer_1_out), .CLR(CLR), .CLK(CLK_t), .EN(EN), .Q(PC));
  // Probe on imm_I
  // Probe on PC
  // Probe on rs1
  // Probe on rs2
  // Probe on rd
  Add #(.Bits(64)) add_1 (.a(PC), .b(64'h4), .c_i(1'b0), .s(add_1_s));  // open: c_o
  // Probe on x0
  // Probe on x1
  // Probe on x2
  // Probe on x3
  // Probe on x4
  // Probe on x5
  inst_mem inst_mem_1 (.PROG(PROG), .ADDR(PC[9:2]), .IW(iw));
  // Probe on x6
  // Probe on x7
  // Probe on x8
  // Probe on x9
  // Probe on A0
  // Probe on A1
  instruction_decoder_part2 instruction_decoder_part2_1 (
    .IW(iw), .WDsel(WDsel), .PCsel(PCsel), .ALUSrcB(ALUSrcB), .ALUSrcA(ALUSrcA), .ALUOp(ALUOp), .RFW(RFW),
    .BROp(BROp), .MSZ(MSZ), .ST(ST), .LD(LD), .MR(MR));
  register_decoder register_decoder_1 (.IW(iw), .RD(rd), .RS1(rs1), .RS2(rs2));
  immediate_decoder immediate_decoder_1 (
    .IW(iw), .imm_I(imm_I), .imm_S(imm_S), .imm_U(imm_U), .imm_B(imm_B), .imm_J(imm_J));
  // Probe on A2
  // Probe on x13
  // Probe on x14
  // Probe on x15
  // Probe on x16
  // Probe on x17
  Multiplexer #(.Bits(64)) multiplexer_2 (
    .sel(WDsel), .in_0(multiplexer_5_out), .in_1(add_1_s), .out(multiplexer_2_out));
  and and_2 (and_2_out, RFW, EN);
  // Probe on x18
  // Probe on x19
  // Probe on x20
  // Probe on x21
  // Probe on x22
  // Probe on x23
  register_file register_file_1 (
    .RR0(rs1), .RR1(rs2), .WR(rd), .WE(and_2_out), .WriteData(multiplexer_2_out), .CLK(CLK_t), .CLR(CLR),
    .R0(A), .R1(B), .x0(x0), .x1(x1), .x2(x2), .x3(x3), .x4(x4), .x5(x5), .x6(x6), .x7(x7), .x8(x8), .x9(x9),
    .x10(A0), .x11(A1), .x12(A2), .x13(x13), .x14(x14), .x15(x15), .x16(x16), .x17(x17), .x18(x18),
    .x19(x19), .x20(x20), .x21(x21), .x22(x22), .x23(x23), .x24(x24), .x25(x25), .x26(x26), .x27(x27),
    .x28(x28), .x29(x29), .x30(x30), .x31(x31));
  // Probe on x24
  // Probe on x25
  // Probe on x26
  // Probe on x27
  // Probe on x28
  // Probe on x29
  // Probe on A
  // Probe on B
  Multiplexer #(.Bits(64)) multiplexer_3 (.sel(ALUSrcA), .in_0(A), .in_1(PC), .out(multiplexer_3_out));
  // Probe on B
  // Probe on ALUSrcB
  Multiplexer #(.Selector_Bits(3), .Bits(64)) multiplexer_4 (
    .sel(ALUSrcB), .in_0(B), .in_1(imm_I), .in_2(imm_J), .in_3(imm_S), .in_4(imm_B), .in_5(imm_U),
    .in_6({64{1'b0}}), .in_7({64{1'b0}}), .out(multiplexer_4_out));
  alu alu_1 (.A(multiplexer_3_out), .B(multiplexer_4_out), .ALUop(ALUOp), .R(alu_1_r));
  // Probe on MR
  Multiplexer #(.Bits(64)) multiplexer_5 (.sel(MR), .in_0(alu_1_r), .in_1(read_1_dout), .out(multiplexer_5_out));
  write write_1 (.A(alu_1_r), .Dcur(read_1_dcur), .MSZ(MSZ), .Data(B), .D(write_1_d));
  RAMDualPort #(.AddrBits(24), .Bits(64)) ramdualport_1 (
    .A(alu_1_r[26:3]), .Din(write_1_d), .str(ST), .C(CLK_t), .ld(LD), .D(ramdualport_1_d));
  // Probe on MSZ
  read read_1 (.MSZ(MSZ), .A(alu_1_r), .D(ramdualport_1_d), .DOUT(read_1_dout), .DCur(read_1_dcur));

  // Other names for the same wires on the sheet: x10[63:0] = A0; x11[63:0] = A1; x12[63:0] = A2

  // Notes on the sheet:
  //   End?
  //   PC+4
endmodule

/* Test case 00-add-r-test:
CLR EN CLK PROG A2
1   0   0   x    x
0   0   0   x    x
while (!(DONE))
0   1   C   0    x
end while
0   1   0   0    3
*/

/* Test case 08-jal-test:
EN CLR CLK PROG A0
1  1   0   x    x
1  0   0   x    x
while (!(DONE))
1  0   C   8    x
end while
1  0   0   8    3
*/

/* Test case 15-sb-lb-test:
CLR EN CLK PROG A0
1   0   0   x    x
0   0   0   x    x
while (!(DONE))
0   1   C   15    x
end while
0   1   0   15    99
*/

/* Test case 01-add-i-test:
CLR EN CLK PROG A2
1   0   0   x    x
0   0   0   x    x
while (!(DONE))
0   1   C   1    x
end while
0   1   1   1    3
*/

/* Test case 09-j-test:
EN CLR CLK PROG A0
1  1   0   x    x
1  0   0   x    x
while (!(DONE))
1  0   C   9    x
end while
1  0   0   9    1
*/

/* Test case 10-beq-test:
EN CLR CLK PROG A0
1  1   0   x    x
1  0   0   x    x
while (!(DONE))
1  0   C   10   x
end while
1  0   0   10   1
*/

/* Test case 06-sd-ld-test:
CLR EN CLK PROG A0
1   0   0   x    x
0   0   0   x    x
while (!(DONE))
0   1   C   6    x
end while
0   1   0   6    99
*/

/* Test case 02-sll-r-test:
CLR EN CLK PROG A0
1   0   0   x    x
0   0   0   x    x
while (!(DONE))
0   1   C   2    x
end while
0   1   0   2    4
*/

/* Test case 11-blt-test:
EN CLR CLK PROG A0
1  1   0   x    x
1  0   0   x    x
while (!(DONE))
1  0   C   11   x
end while
1  0   0   11   1
*/

/* Test case 07-sw-lw-test:
CLR EN CLK PROG A0
1   0   0   x    x
0   0   0   x    x
while (!(DONE))
0   1   C   7    x
end while
0   1   0   7    99
*/

/* Test case 21-to-upper-test:
CLR EN CLK PROG A0
1   0   0   x    x
0   0   0   x    x
while (!(DONE))
0   1   C   21   x
end while
0   1   0   21   5066355251797426176
*/

/* Test case 03-sll-i-test:
CLR EN CLK PROG A0
1   0   0   x    x
0   0   0   x    x
while (!(DONE))
0   1   C   3    x
end while
0   1   0   3    8
*/

/* Test case 12-bge-test:
EN CLR CLK PROG A0
1  1   0   x    x
1  0   0   x    x
while (!(DONE))
1  0   C   12   x
end while
1  0   0   12   2
*/

/* Test case 04-srl-r-test:
CLR EN CLK PROG A0
1   0   0   x    x
0   0   0   x    x
while (!(DONE))
0   1   C   4    x
end while
0   1   0   4    4
*/

/* Test case 17-get-bitseq-test:
CLR EN CLK PROG A0
1   0   0   x    x
0   0   0   x    x
while (!(DONE))
0   1   C   17   x
end while
0   1   0   17   6
*/

/* Test case 05-srl-i-test:
CLR EN CLK PROG A0
1   0   0   x    x
0   0   0   x    x
while (!(DONE))
0   1   C   5    x
end while
0   1   0   5    8
*/

/* Test case 13-mul-test:
EN CLR CLK PROG A0
1  1   0   x    x
1  0   0   x    x
while (!(DONE))
1  0   C   13   x
end while
1  0   0   13   9
*/

/* Test case 19-fib-rec-test:
CLR EN CLK PROG A0
1   0   0   x    x
0   0   0   x    x
while (!(DONE))
0   1   C   19   x
end while
0   1   0   19   55
*/

/* Test case 14-lui-test:
EN CLR CLK PROG A0
1  1   0   x    x
1  0   0   x    x
while (!(DONE))
1  0   C   14   x
end while
1  0   0   14   4096
*/
