// Digital circuit read.dig as structural Verilog
module read (
  input  [63:0] D,
  input  [63:0] A,
  input  [1:0] MSZ,
  output [63:0] DCur,
  output [63:0] DOUT
);

  wire [7:0] multiplexer_2_out;
  wire [31:0] multiplexer_1_out;
  wire [63:0] bitextender_1_out, bitextender_2_out;

  Multiplexer #(.Bits(32)) multiplexer_1 (.sel(A[2]), .in_0(D[31:0]), .in_1(D[63:32]), .out(multiplexer_1_out));
  Multiplexer #(.Selector_Bits(3), .Bits(8)) multiplexer_2 (
    .sel(A[2:0]), .in_0(D[7:0]), .in_1(D[15:8]), .in_2(D[23:16]), .in_3(D[31:24]), .in_4(D[39:32]),
    .in_5(D[47:40]), .in_6(D[55:48]), .in_7(D[63:56]), .out(multiplexer_2_out));
  BitExtender #(.inputBits(32), .outputBits(64)) bitextender_1 (.in(multiplexer_1_out), .out(bitextender_1_out));
  BitExtender #(.outputBits(64)) bitextender_2 (.in(multiplexer_2_out), .out(bitextender_2_out));
  Multiplexer #(.Selector_Bits(2), .Bits(64)) multiplexer_3 (
    .sel(MSZ), .in_0({64{1'b0}}), .in_1(bitextender_2_out), .in_2(bitextender_1_out), .in_3(D), .out(DOUT));

  assign DCur = D;

  // Other names for the same wires on the sheet: bidx[2:0] = A[2:0]; widx = A[2]; b0[7:0] = D[7:0]; b1[7:0] = D[15:8];
  //   b2[7:0] = D[23:16]; b3[7:0] = D[31:24]; b4[7:0] = D[39:32]; b5[7:0] = D[47:40]; b6[7:0] = D[55:48];
  //   b7[7:0] = D[63:56]
endmodule
