// Digital circuit register_decoder.dig as structural Verilog
module register_decoder (
  input  [31:0] IW,
  output [4:0] RD,
  output [4:0] RS1,
  output [4:0] RS2
);


  assign RD = IW[11:7];
  assign RS1 = IW[19:15];
  assign RS2 = IW[24:20];
endmodule
