// Digital circuit register_file.dig as structural Verilog
module register_file (
  input  [4:0] WR,
  input  [63:0] WriteData,
  input  CLK,
  input  CLR,
  input  WE,
  input  [4:0] RR1,
  input  [4:0] RR0,
  output [63:0] R0,
  output [63:0] R1,
  output [63:0] x0,
  output [63:0] x1,
  output [63:0] x2,
  output [63:0] x3,
  output [63:0] x4,
  output [63:0] x5,
  output [63:0] x6,
  output [63:0] x7,
  output [63:0] x8,
  output [63:0] x9,
  output [63:0] x10,
  output [63:0] x11,
  output [63:0] x12,
  output [63:0] x13,
  output [63:0] x14,
  output [63:0] x15,
  output [63:0] x16,
  output [63:0] x17,
  output [63:0] x18,
  output [63:0] x19,
  output [63:0] x20,
  output [63:0] x21,
  output [63:0] x22,
  output [63:0] x23,
  output [63:0] x24,
  output [63:0] x25,
  output [63:0] x26,
  output [63:0] x27,
  output [63:0] x28,
  output [63:0] x29,
  output [63:0] x30,
  output [63:0] x31
);

  wire EN1, EN2, EN3, EN4, EN5, EN6, EN7, EN8, EN9, EN10, EN11, EN12, EN13, EN14, EN15, EN16, EN17, EN18,
       EN19, EN20, EN21, EN22, EN23, EN24, EN25, EN26, EN27, EN28, EN29, EN30, EN31;
  wire [4:0] multiplexer_1_out;

  Multiplexer #(.Bits(5)) multiplexer_1 (.sel(WE), .in_0({5{1'b0}}), .in_1(WR), .out(multiplexer_1_out));
  Decoder #(.Selector_Bits(5)) decoder_1 (
    .sel(multiplexer_1_out), .out_1(EN1), .out_2(EN2), .out_3(EN3), .out_4(EN4), .out_5(EN5), .out_6(EN6),
    .out_7(EN7), .out_8(EN8), .out_9(EN9), .out_10(EN10), .out_11(EN11), .out_12(EN12), .out_13(EN13),
    .out_14(EN14), .out_15(EN15), .out_16(EN16), .out_17(EN17), .out_18(EN18), .out_19(EN19), .out_20(EN20),
    .out_21(EN21), .out_22(EN22), .out_23(EN23), .out_24(EN24), .out_25(EN25), .out_26(EN26), .out_27(EN27),
    .out_28(EN28), .out_29(EN29), .out_30(EN30), .out_31(EN31));  // open: out_0
  _64bit_register _64bit_register_1 (.D(WriteData), .CLR(CLR), .CLK(CLK), .EN(EN1), .Q(x1));
  _64bit_register _64bit_register_2 (.D(WriteData), .CLR(CLR), .CLK(CLK), .EN(EN2), .Q(x2));
  _64bit_register _64bit_register_3 (.D(WriteData), .CLR(CLR), .CLK(CLK), .EN(EN3), .Q(x3));
  _64bit_register _64bit_register_4 (.D(WriteData), .CLR(CLR), .CLK(CLK), .EN(EN4), .Q(x4));
  _64bit_register _64bit_register_5 (.D(WriteData), .CLR(CLR), .CLK(CLK), .EN(EN5), .Q(x5));
  _64bit_register _64bit_register_6 (.D(WriteData), .CLR(CLR), .CLK(CLK), .EN(EN6), .Q(x6));
  _64bit_register _64bit_register_7 (.D(WriteData), .CLR(CLR), .CLK(CLK), .EN(EN7), .Q(x7));
  _64bit_register _64bit_register_8 (.D(WriteData), .CLR(CLR), .CLK(CLK), .EN(EN8), .Q(x8));
  _64bit_register _64bit_register_9 (.D(WriteData), .CLR(CLR), .CLK(CLK), .EN(EN9), .Q(x9));
  _64bit_register _64bit_register_10 (.D(WriteData), .CLR(CLR), .CLK(CLK), .EN(EN10), .Q(x10));
  _64bit_register _64bit_register_11 (.D(WriteData), .CLR(CLR), .CLK(CLK), .EN(EN11), .Q(x11));
  _64bit_register _64bit_register_12 (.D(WriteData), .CLR(CLR), .CLK(CLK), .EN(EN12), .Q(x12));
  _64bit_register _64bit_register_13 (.D(WriteData), .CLR(CLR), .CLK(CLK), .EN(EN13), .Q(x13));
  _64bit_register _64bit_register_14 (.D(WriteData), .CLR(CLR), .CLK(CLK), .EN(EN14), .Q(x14));
  _64bit_register _64bit_register_15 (.D(WriteData), .CLR(CLR), .CLK(CLK), .EN(EN15), .Q(x15));
  _64bit_register _64bit_register_16 (.D(WriteData), .CLR(CLR), .CLK(CLK), .EN(EN16), .Q(x16));
  _64bit_register _64bit_register_17 (.D(WriteData), .CLR(CLR), .CLK(CLK), .EN(EN17), .Q(x17));
  _64bit_register _64bit_register_18 (.D(WriteData), .CLR(CLR), .CLK(CLK), .EN(EN18), .Q(x18));
  _64bit_register _64bit_register_19 (.D(WriteData), .CLR(CLR), .CLK(CLK), .EN(EN19), .Q(x19));
  _64bit_register _64bit_register_20 (.D(WriteData), .CLR(CLR), .CLK(CLK), .EN(EN20), .Q(x20));
  _64bit_register _64bit_register_21 (.D(WriteData), .CLR(CLR), .CLK(CLK), .EN(EN21), .Q(x21));
  _64bit_register _64bit_register_22 (.D(WriteData), .CLR(CLR), .CLK(CLK), .EN(EN22), .Q(x22));
  _64bit_register _64bit_register_23 (.D(WriteData), .CLR(CLR), .CLK(CLK), .EN(EN23), .Q(x23));
  _64bit_register _64bit_register_24 (.D(WriteData), .CLR(CLR), .CLK(CLK), .EN(EN24), .Q(x24));
  _64bit_register _64bit_register_25 (.D(WriteData), .CLR(CLR), .CLK(CLK), .EN(EN25), .Q(x25));
  _64bit_register _64bit_register_26 (.D(WriteData), .CLR(CLR), .CLK(CLK), .EN(EN26), .Q(x26));
  _64bit_register _64bit_register_27 (.D(WriteData), .CLR(CLR), .CLK(CLK), .EN(EN27), .Q(x27));
  _64bit_register _64bit_register_28 (.D(WriteData), .CLR(CLR), .CLK(CLK), .EN(EN28), .Q(x28));
  _64bit_register _64bit_register_29 (.D(WriteData), .CLR(CLR), .CLK(CLK), .EN(EN29), .Q(x29));
  _64bit_register _64bit_register_30 (.D(WriteData), .CLR(CLR), .CLK(CLK), .EN(EN30), .Q(x30));
  _64bit_register _64bit_register_31 (.D(WriteData), .CLR(CLR), .CLK(CLK), .EN(EN31), .Q(x31));
  Multiplexer #(.Selector_Bits(5), .Bits(64)) multiplexer_2 (
    .sel(RR1), .in_0({64{1'b0}}), .in_1(x1), .in_2(x2), .in_3(x3), .in_4(x4), .in_5(x5), .in_6(x6),
    .in_7(x7), .in_8(x8), .in_9(x9), .in_10(x10), .in_11(x11), .in_12(x12), .in_13(x13), .in_14(x14),
    .in_15(x15), .in_16(x16), .in_17(x17), .in_18(x18), .in_19(x19), .in_20(x20), .in_21(x21), .in_22(x22),
    .in_23(x23), .in_24(x24), .in_25(x25), .in_26(x26), .in_27(x27), .in_28(x28), .in_29(x29), .in_30(x30),
    .in_31(x31), .out(R1));
  Multiplexer #(.Selector_Bits(5), .Bits(64)) multiplexer_3 (
    .sel(RR0), .in_0({64{1'b0}}), .in_1(x1), .in_2(x2), .in_3(x3), .in_4(x4), .in_5(x5), .in_6(x6),
    .in_7(x7), .in_8(x8), .in_9(x9), .in_10(x10), .in_11(x11), .in_12(x12), .in_13(x13), .in_14(x14),
    .in_15(x15), .in_16(x16), .in_17(x17), .in_18(x18), .in_19(x19), .in_20(x20), .in_21(x21), .in_22(x22),
    .in_23(x23), .in_24(x24), .in_25(x25), .in_26(x26), .in_27(x27), .in_28(x28), .in_29(x29), .in_30(x30),
    .in_31(x31), .out(R0));

  assign x0 = {64{1'b0}};

  // Other names for the same wires on the sheet: D[63:0] = WriteData
endmodule
