// Digital circuit write.dig as structural Verilog
module write (
  input  [1:0] MSZ,
  input  [63:0] Data,
  input  [63:0] Dcur,
  input  [63:0] A,
  output [63:0] D
);

  wire [63:0] multiplexer_1_out, multiplexer_2_out;

  Multiplexer #(.Selector_Bits(3), .Bits(64)) multiplexer_1 (
    .sel(A[2:0]), .in_0({Dcur[63:8], Data[7:0]}), .in_1({Dcur[63:16], Data[7:0], Dcur[7:0]}),
    .in_2({Dcur[63:24], Data[7:0], Dcur[15:0]}), .in_3({Dcur[63:32], Data[7:0], Dcur[23:0]}),
    .in_4({Dcur[63:40], Data[7:0], Dcur[31:0]}), .in_5({Dcur[63:48], Data[7:0], Dcur[39:0]}),
    .in_6({Dcur[63:56], Data[7:0], Dcur[47:0]}), .in_7({Data[7:0], Dcur[55:0]}), .out(multiplexer_1_out));
  Multiplexer #(.Bits(64)) multiplexer_2 (
    .sel(A[2]), .in_0({Dcur[63:32], Data[31:0]}), .in_1({Data[31:0], Dcur[31:0]}), .out(multiplexer_2_out));
  Multiplexer #(.Selector_Bits(2), .Bits(64)) multiplexer_3 (
    .sel(MSZ), .in_0({64{1'b0}}), .in_1(multiplexer_1_out), .in_2(multiplexer_2_out), .in_3(Data), .out(D));

  // Other names for the same wires on the sheet: bidx[2:0] = A[2:0]; widx = A[2]; bnew[7:0] = Data[7:0];
  //   wnew[31:0] = Data[31:0]; b0[7:0] = Dcur[7:0]; w0[31:0] = Dcur[31:0]; b1[7:0] = Dcur[15:8];
  //   b2[7:0] = Dcur[23:16]; b3[7:0] = Dcur[31:24]; b4[7:0] = Dcur[39:32]; w1[31:0] = Dcur[63:32];
  //   b5[7:0] = Dcur[47:40]; b6[7:0] = Dcur[55:48]; b7[7:0] = Dcur[63:56]
endmodule
